// Logisim project 32.circ as structural Verilog
module main (
  input  [31:0] in_1,
  input  [3:0] in_2,
  output out_3,
  output [31:0] out_4
);

  Core_0 core_0_1 (.in_1(in_1), .out_4(out_4), .INPUT_OUTPUT(out_3), .in_3(in_2));  // open: in_2
  Core_1 core_1_1 ();
  L1_Cache l1_cache_1 ();
  L1_Cache l1_cache_2 ();
  L2_Cache l2_cache_1 ();
  L3_Cache l3_cache_1 ();
  Core_2 core_2_1 ();
  Core_3 core_3_1 ();
  L1_Cache l1_cache_3 ();
  L1_Cache l1_cache_4 ();
  L2_Cache l2_cache_2 ();
endmodule

module Core_0 (
  input  [31:0] in_1,
  input  [3:0] in_2,
  input  [3:0] in_3,
  output [31:0] out_4,
  output INPUT_OUTPUT
);

  wire bit_extender_1_out, undriven_4, undriven_7, undriven_8, undriven_9;
  wire [8:0] undriven;
  wire [31:0] A_q, B_q, register_1_q, register_2_q, register_3_q, register_4_q, undriven_2, undriven_3,
       undriven_5, undriven_6;

  ALU alu_1 (.A(A_q), .in_3(in_2), .B(B_q), .out_4(in_1));
  Control_Unit control_unit_1 ();  // open: CLK, INSTRUCTIONS, out_3
  Register_part #(.width(32)) register_1 (
    .D(in_1), .en(undriven[7]), .Q(register_1_q), .clk(undriven[8]), .clr(undriven[6]));
  assign in_1 = register_1_q & undriven_2;  // AND_Gate and_1, 32 bits wide
  Register_part #(.width(32)) register_2 (
    .D(in_1), .en(undriven[5]), .Q(register_2_q), .clk(undriven[8]), .clr(undriven[4]));
  Register_part #(.width(32)) register_3 (
    .D(in_1), .en(undriven[3]), .Q(register_3_q), .clk(undriven[8]), .clr(undriven[2]));
  assign in_1 = register_2_q & undriven_3;  // AND_Gate and_2, 32 bits wide
  assign in_1 = register_3_q & undriven_5;  // AND_Gate and_3, 32 bits wide
  Register_part #(.width(32)) register_4 (
    .D(in_1), .en(undriven[1]), .Q(register_4_q), .clk(undriven[8]), .clr(undriven[0]));
  assign in_1 = register_4_q & undriven_6;  // AND_Gate and_4, 32 bits wide
  Register_part #(.width(32)) A (.D(in_1), .en(undriven_4), .Q(A_q), .clk(undriven[8]), .clr(undriven_7));
  Bit_Extender #(.in_width(4), .out_width(1)) bit_extender_1 (.in(in_3), .out(bit_extender_1_out));
  _4T1 u_4t1_1 ();  // open: in_1, in_2, out_3, out_4
  Register_part #(.width(32)) B (.D(in_1), .en(undriven_8), .Q(B_q), .clk(undriven[8]), .clr(undriven_9));

  assign out_4 = in_1;
endmodule

module ALU (
  input  [31:0] A,
  input  [31:0] B,
  input  [3:0] in_3,
  output [31:0] out_4
);

  wire arithmatic_functions_1_f_carry;
  wire [4:0] bit_extender_1_out, bit_extender_2_out;
  wire [31:0] arithmatic_functions_1_add_a_2, arithmatic_functions_1_div_a_2, arithmatic_functions_1_div_rem,
       arithmatic_functions_1_mult_a_2, arithmatic_functions_1_mult_carry, arithmatic_functions_1_sub_a_2,
       bit_extender_3_out, dec_1_out_2, demultiplexer_1_out1, demultiplexer_1_out2, demultiplexer_1_out3,
       demultiplexer_1_out4, demultiplexer_1_out5, demultiplexer_1_out6, demultiplexer_1_out7,
       demultiplexer_1_out8, demultiplexer_1_out9, demultiplexer_1_out10, demultiplexer_1_out11,
       demultiplexer_1_out12, demultiplexer_2_out1, demultiplexer_2_out2, demultiplexer_2_out3,
       demultiplexer_2_out4, demultiplexer_2_out5, demultiplexer_2_out6, demultiplexer_2_out7,
       demultiplexer_2_out8, demultiplexer_2_out9, demultiplexer_2_out10, demultiplexer_2_out11,
       demultiplexer_2_out12, inc_1_out_2, logic_funcs_1_and, logic_funcs_1_not_2, logic_funcs_1_or,
       logic_funcs_1_xor, shifter_1_out, shifter_2_out;

  Demultiplexer #(.select(4), .width(32), .disabled(0)) demultiplexer_1 (
    .out1(demultiplexer_1_out1), .out2(demultiplexer_1_out2), .out3(demultiplexer_1_out3),
    .out4(demultiplexer_1_out4), .out5(demultiplexer_1_out5), .out6(demultiplexer_1_out6),
    .out7(demultiplexer_1_out7), .out8(demultiplexer_1_out8), .out9(demultiplexer_1_out9),
    .out10(demultiplexer_1_out10), .out11(demultiplexer_1_out11), .out12(demultiplexer_1_out12), .in(A),
    .sel(in_3));  // open: out0, out13, out14, out15, en
  Demultiplexer #(.select(4), .width(32), .disabled(0)) demultiplexer_2 (
    .out1(demultiplexer_2_out1), .out2(demultiplexer_2_out2), .out3(demultiplexer_2_out3),
    .out4(demultiplexer_2_out4), .out5(demultiplexer_2_out5), .out6(demultiplexer_2_out6),
    .out7(demultiplexer_2_out7), .out8(demultiplexer_2_out8), .out9(demultiplexer_2_out9),
    .out10(demultiplexer_2_out10), .out11(demultiplexer_2_out11), .out12(demultiplexer_2_out12), .in(B),
    .sel(in_3));  // open: out0, out13, out14, out15, en
  Bit_Extender #(.in_width(32), .out_width(5)) bit_extender_1 (.in(demultiplexer_2_out9), .out(bit_extender_1_out));
  Bit_Extender #(.in_width(32), .out_width(5)) bit_extender_2 (.in(demultiplexer_2_out10), .out(bit_extender_2_out));
  Arithmatic_functions arithmatic_functions_1 (
    .ADD_A(demultiplexer_1_out1), .ADD_B(demultiplexer_2_out1), .SUB_A(demultiplexer_1_out2),
    .SUB_B(demultiplexer_2_out2), .MULT_A(demultiplexer_1_out3), .MULT_B(demultiplexer_2_out3),
    .DIV_A(demultiplexer_1_out4), .DIV_B(demultiplexer_2_out4), .ADD_A_2(arithmatic_functions_1_add_a_2),
    .SUB_A_2(arithmatic_functions_1_sub_a_2), .MULT_A_2(arithmatic_functions_1_mult_a_2),
    .DIV_A_2(arithmatic_functions_1_div_a_2), .F_CARRY(arithmatic_functions_1_f_carry),
    .MULT_CARRY(arithmatic_functions_1_mult_carry), .DIV_REM(arithmatic_functions_1_div_rem));
  LOGIC_FUNCS logic_funcs_1 (
    .AND_A(demultiplexer_1_out5), .AND_B(demultiplexer_2_out5), .OR_A(demultiplexer_1_out6),
    .OR_B(demultiplexer_2_out6), .XOR_A(demultiplexer_1_out7), .XOR_B(demultiplexer_2_out7),
    .NOT(demultiplexer_1_out8), .AND(logic_funcs_1_and), .OR(logic_funcs_1_or), .XOR(logic_funcs_1_xor),
    .NOT_2(logic_funcs_1_not_2));
  Shifter #(.width(32)) shifter_1 (.in(demultiplexer_1_out9), .\dist (bit_extender_1_out), .out(shifter_1_out));
  Shifter #(.width(32), .shift("lr")) shifter_2 (
    .in(demultiplexer_1_out10), .\dist (bit_extender_2_out), .out(shifter_2_out));
  INC inc_1 (.in_1(demultiplexer_1_out11), .out_2(inc_1_out_2));
  DEC dec_1 (.in_1(demultiplexer_1_out12), .out_2(dec_1_out_2));
  ALU_INF alu_inf_1 (
    .in_1(dec_1_out_2), .in_2(inc_1_out_2), .in_3(shifter_2_out), .in_4(shifter_1_out),
    .in_5(logic_funcs_1_not_2), .in_6(logic_funcs_1_or), .in_7(logic_funcs_1_and),
    .in_8(arithmatic_functions_1_div_a_2), .in_9(arithmatic_functions_1_sub_a_2),
    .in_10(arithmatic_functions_1_add_a_2));
  assign bit_extender_3_out = {{31{1'b0}}, arithmatic_functions_1_f_carry};  // Bit_Extender bit_extender_3
  assign out_4 = arithmatic_functions_1_add_a_2 | arithmatic_functions_1_sub_a_2 | arithmatic_functions_1_mult_a_2 | arithmatic_functions_1_div_a_2 | logic_funcs_1_and | logic_funcs_1_or | logic_funcs_1_xor | logic_funcs_1_not_2 | shifter_1_out | shifter_2_out | inc_1_out_2 | dec_1_out_2 | arithmatic_functions_1_mult_carry | arithmatic_functions_1_div_rem | bit_extender_3_out;  // OR_Gate or_1, 32 bits wide
endmodule

// CONTROL_UNIT
module Control_Unit (
  input  [31:0] INSTRUCTIONS,
  output CLK,
  output [3:0] out_3
);

  wire if_1_out_2;

  Clock clock_1 (.out(CLK));
  Counter #(.width(32), .max('hffffffff)) SQC (.clk(CLK));  // open: load, D, count, Q, carry, clr
  IF if_1 (.in_1(INSTRUCTIONS[3:0]), .out_2(if_1_out_2));
  CTRL_LOGIC ctrl_logic_1 (.HLT(if_1_out_2));  // open: LOAD

  assign out_3 = INSTRUCTIONS[3:0];
endmodule

// REG
module Register (
);

  Register_part #(.width(32)) register_1 ();  // open: D, en, Q, clk, clr
endmodule

// ARTH_FUNCS
module Arithmatic_functions (
  input  [31:0] ADD_A,
  input  [31:0] ADD_B,
  input  [31:0] SUB_A,
  input  [31:0] SUB_B,
  input  [31:0] MULT_A,
  input  [31:0] MULT_B,
  input  [31:0] DIV_A,
  input  [31:0] DIV_B,
  output [31:0] ADD_A_2,
  output [31:0] SUB_A_2,
  output [31:0] MULT_A_2,
  output [31:0] DIV_A_2,
  output F_CARRY,
  output [31:0] MULT_CARRY,
  output [31:0] DIV_REM
);

  wire adder_1_cout, subtractor_1_bout;

  Adder #(.width(32)) adder_1 (.a(ADD_A), .b(ADD_B), .out(ADD_A_2), .cout(adder_1_cout));  // open: cin
  Subtractor #(.width(32)) subtractor_1 (.a(SUB_A), .b(SUB_B), .out(SUB_A_2), .bout(subtractor_1_bout));  // open: bin
  Multiplier #(.width(32)) multiplier_1 (.a(MULT_A), .b(MULT_B), .out(MULT_A_2), .cout(MULT_CARRY));  // open: cin
  Divider #(.width(32)) divider_1 (.a(DIV_A), .b(DIV_B), .out(DIV_A_2), .rem(DIV_REM));  // open: upper
  or or_1 (F_CARRY, adder_1_cout, subtractor_1_bout);
endmodule

module ALU_INF (
  input  [31:0] in_1,
  input  [31:0] in_2,
  input  [31:0] in_3,
  input  [31:0] in_4,
  input  [31:0] in_5,
  input  [31:0] in_6,
  input  [31:0] in_7,
  input  [31:0] in_8,
  input  [31:0] in_9,
  input  [31:0] in_10
);

  wire or_1_out, or_2_out, or_3_out, or_4_out, or_5_out, or_6_out, or_7_out, or_8_out, or_9_out, or_10_out,
       or_11_out, or_12_out, or_13_out, or_14_out, or_15_out, or_16_out, or_17_out, or_18_out, or_19_out,
       or_20_out, or_21_out, or_22_out, or_23_out, or_24_out, or_25_out, or_26_out, or_27_out, or_28_out,
       or_29_out, or_30_out, or_31_out;
  wire [31:0] nor_1_out, nor_2_out, nor_3_out, nor_4_out, nor_5_out, nor_6_out, nor_7_out, nor_8_out,
       nor_9_out;

  assign nor_1_out = ~(in_1 | in_3);  // NOR_Gate nor_1, 32 bits wide
  assign nor_2_out = ~(nor_1_out | nor_3_out);  // NOR_Gate nor_2, 32 bits wide
  assign nor_3_out = ~(in_2 | in_4);  // NOR_Gate nor_3, 32 bits wide
  assign nor_4_out = ~(in_5 | in_6);  // NOR_Gate nor_4, 32 bits wide
  assign nor_5_out = ~(in_7 | in_9);  // NOR_Gate nor_5, 32 bits wide
  assign nor_6_out = ~(nor_5_out | nor_7_out);  // NOR_Gate nor_6, 32 bits wide
  assign nor_7_out = ~(in_8 | in_10);  // NOR_Gate nor_7, 32 bits wide
  Bit_Extender #(.in_width(32), .out_width(1)) bit_extender_1 ();  // open: in, out
  Bit_Extender #(.in_width(32), .out_width(1)) bit_extender_2 ();  // open: in, out
  assign nor_8_out = ~(nor_2_out | nor_9_out);  // NOR_Gate nor_8, 32 bits wide
  assign nor_9_out = ~(nor_4_out | nor_6_out);  // NOR_Gate nor_9, 32 bits wide
  Bit_Extender #(.in_width(32), .out_width(1)) bit_extender_3 ();  // open: in, out
  or or_1 (or_1_out, nor_8_out[0], nor_8_out[2]);
  or or_2 (or_2_out, nor_8_out[1], nor_8_out[3]);
  or or_3 (or_3_out, nor_8_out[4], nor_8_out[6]);
  or or_4 (or_4_out, nor_8_out[5], nor_8_out[7]);
  or or_5 (or_5_out, nor_8_out[8], nor_8_out[10]);
  or or_6 (or_6_out, nor_8_out[9], nor_8_out[11]);
  or or_7 (or_7_out, nor_8_out[12], nor_8_out[14]);
  or or_8 (or_8_out, nor_8_out[13], nor_8_out[15]);
  or or_9 (or_9_out, nor_8_out[16], nor_8_out[18]);
  or or_10 (or_10_out, nor_8_out[17], nor_8_out[19]);
  or or_11 (or_11_out, nor_8_out[20], nor_8_out[22]);
  or or_12 (or_12_out, nor_8_out[21], nor_8_out[23]);
  or or_13 (or_13_out, nor_8_out[24], nor_8_out[26]);
  or or_14 (or_14_out, nor_8_out[25], nor_8_out[27]);
  or or_15 (or_15_out, nor_8_out[28], nor_8_out[30]);
  or or_16 (or_16_out, nor_8_out[29], nor_8_out[31]);
  or or_17 (or_17_out, or_1_out, or_3_out);
  or or_18 (or_18_out, or_2_out, or_4_out);
  or or_19 (or_19_out, or_5_out, or_7_out);
  or or_20 (or_20_out, or_6_out, or_8_out);
  or or_21 (or_21_out, or_9_out, or_11_out);
  or or_22 (or_22_out, or_10_out, or_12_out);
  or or_23 (or_23_out, or_13_out, or_15_out);
  or or_24 (or_24_out, or_14_out, or_16_out);
  or or_25 (or_25_out, or_17_out, or_19_out);
  or or_26 (or_26_out, or_18_out, or_20_out);
  or or_27 (or_27_out, or_21_out, or_23_out);
  or or_28 (or_28_out, or_22_out, or_24_out);
  or or_29 (or_29_out, or_25_out, or_27_out);
  or or_30 (or_30_out, or_26_out, or_28_out);
  or or_31 (or_31_out, or_29_out, or_30_out);
endmodule

module LOGIC_FUNCS (
  input  [31:0] AND_A,
  input  [31:0] AND_B,
  input  [31:0] OR_A,
  input  [31:0] OR_B,
  input  [31:0] XOR_A,
  input  [31:0] XOR_B,
  input  [31:0] NOT,
  output [31:0] AND,
  output [31:0] OR,
  output [31:0] XOR,
  output [31:0] NOT_2
);

  assign AND = AND_A & AND_B;  // AND_Gate and_1, 32 bits wide
  assign OR = OR_A | OR_B;  // OR_Gate or_1, 32 bits wide
  assign XOR = XOR_A ^ XOR_B;  // XOR_Gate xor_1, 32 bits wide
  assign NOT_2 = ~NOT;  // NOT_Gate not_1, 32 bits wide
endmodule

module INC (
  input  [31:0] in_1,
  output [31:0] out_2
);

  Adder #(.width(32)) adder_1 (.a(32'h1), .b(in_1), .out(out_2));  // open: cin, cout
endmodule

module DEC (
  input  [31:0] in_1,
  output [31:0] out_2
);

  Subtractor #(.width(32)) subtractor_1 (.a(32'h1), .b(in_1), .out(out_2));  // open: bin, bout
endmodule

module CTRL_LOGIC (
  input  HLT,
  input  LOAD
);
endmodule

module IF (
  input  [3:0] in_1,
  output out_2
);

  wire or_1_out;

  or or_1 (or_1_out, in_1[3], in_1[2], in_1[1], in_1[0]);
  not not_1 (out_2, or_1_out);
endmodule

module _4T1 (
  input  [3:0] in_1,
  input  [31:0] in_2,
  output out_3,
  output [31:0] out_4
);


  assign in_1[2:0] = {3{in_1[3]}};
  assign out_3 = in_1[3];
  assign out_4 = in_2;
endmodule
